// Logisim project mimo_LAB_05_Simple_demo_circuit.circ as structural Verilog: 2 circuits, main circuit main
module main (
  input  [3:0] in_1,
  input  [3:0] in_2,
  input  _0____Vsota,
  input  in_4,
  input  in_5,
  output [3:0] out_6,
  output out_7,
  output out_8,
  output out_9
);

  Hex_Digit_Display hex_digit_display_1 (.value(in_1));  // open: dp
  Hex_Digit_Display hex_digit_display_2 (.value(in_2));  // open: dp
  ALE ale_1 (.in_2(in_2), .Selector(_0____Vsota), .in_1(in_1), .out_4(out_6));
  Hex_Digit_Display hex_digit_display_3 (.value(out_6));  // open: dp
  // Probe on out_6
  LedBar #(.matrixcols(4)) ledbar_1 (.led0(out_6[3]), .led1(out_6[2]), .led2(out_6[1]), .led3(out_6[0]));
  not not_1 (out_7, in_4);
  and and_1 (out_8, in_5, in_4);
  or or_1 (out_9, in_4, in_5);

  // Other names for the same wires on the sheet: SEL = _0____Vsota

  // Notes on the sheet:
  //   1 .. Produkt
endmodule

module ALE (
  input  [3:0] in_1,
  input  [3:0] in_2,
  input  Selector,
  output [3:0] out_4
);

  wire [3:0] adder_1_out, multiplier_1_out;

  Adder #(.width(4)) adder_1 (.a(in_1), .b(in_2), .out(adder_1_out));  // open: cin, cout
  Multiplier #(.width(4)) multiplier_1 (.a(in_1), .b(in_2), .out(multiplier_1_out));  // open: cin, cout
  Multiplexer #(.width(4)) multiplexer_1 (.in0(adder_1_out), .in1(multiplier_1_out), .out(out_4), .sel(Selector));
endmodule
