// Logisim project mimo_v04b_AddrBus_Demo.circ as structural Verilog: 2 circuits, main circuit MiMo_v04b_OR
// address
module MiMo_v04b_OR (
  input  [15:0] in_1,
  input  [15:0] IMM,
  input  [15:0] ALUOUT,
  input  [1:0] addrsel,
  input  [15:0] SREG
);

  wire CLK, reset;
  wire [3:0] showhexa_1_digit, showhexa_1_out_3, showhexa_1_out_4, showhexa_1_out_5;
  wire [15:0] address;

  Hex_Digit_Display hex_digit_display_1 (.value(showhexa_1_digit));  // open: dp
  ShowHexa showhexa_1 (
    .out_4(showhexa_1_out_4), .out_5(showhexa_1_out_5), .Digit(showhexa_1_digit), .out_3(showhexa_1_out_3),
    .Data(address));
  Hex_Digit_Display hex_digit_display_2 (.value(showhexa_1_out_4));  // open: dp
  Hex_Digit_Display hex_digit_display_3 (.value(showhexa_1_out_3));  // open: dp
  Hex_Digit_Display hex_digit_display_4 (.value(showhexa_1_out_5));  // open: dp
  // Probe on address
  Multiplexer #(.select(2), .width(16)) multiplexer_1 (
    .in0(in_1), .in1(IMM), .in2(ALUOUT), .in3(SREG), .out(address), .sel(addrsel));
  // Probe on addrsel
  // Probe on in_1
  Clock clock_1 (.out(CLK));
  Button u_Reset (.out(reset));

  // Other names for the same wires on the sheet: immed[15:0] = IMM; pc[15:0] = in_1

  // Notes on the sheet:
  //   Address BUS
  //   MiMo - Microprogrammed CPU Model
  //   addrsel: 0..PC 1..IMM 2..ALU 3..Sreg 
  //   v0.5
  //   OR
  //   PC
endmodule

module ShowHexa (
  input  [15:0] Data,
  output [3:0] Digit,
  output [3:0] out_3,
  output [3:0] out_4,
  output [3:0] out_5
);


  assign Digit = Data[15:12];
  assign out_3 = Data[11:8];
  assign out_4 = Data[7:4];
  assign out_5 = Data[3:0];
endmodule
