// Logisim project mimo_v04b_Control_Unit_Demo.circ as structural Verilog: 1 circuit, main circuit main
module main (
  input  [7:0] Mikro_PC,
  input  Flags,
  input  in_3,
  input  opcode,
  input  [6:0] in_5,
  input  in_6,
  output [7:0] out_7,
  output [7:0] out_8
);

  wire CLK, multiplexer_2_out, Ncmd, or_1_out, reset;
  wire [1:0] addrsel, cond;
  wire [3:0] aluop;
  wire [7:0] multiplexer_1_out, multiplexer_3_out;
  wire [15:0] DROM;
  wire [31:4] CROM;

  nor nor_1 (Ncmd, Mikro_PC[0], Mikro_PC[1], Mikro_PC[2], Mikro_PC[3], Mikro_PC[5], Mikro_PC[6], Mikro_PC[7], Mikro_PC[4]);
  // Probe on Mikro_PC
  // Probe on CROM[21:20]
  LED led_1 (.in(CROM[22]));
  // Probe on Mikro_PC
  // Probe on Mikro_PC
  // Probe on Mikro_PC
  // Probe on cond
  LED led_2 (.in(in_6));
  ROM #(.dataWidth(32)) rom_1 (
    .addr(Mikro_PC), .data({CROM[31:20], in_6, cond, CROM[16:9], addrsel, CROM[6:4], aluop}));
  ROM #(.dataWidth(16)) rom_2 (.addr(Mikro_PC), .data(DROM));
  // Probe on in_5
  // Probe on CROM[16:15]
  LED led_3 (.in(CROM[14]));
  or or_1 (or_1_out, Flags, in_3);
  // Probe on {CROM[31:20], in_6, cond, CROM[16:9], addrsel, CROM[6:4], aluop}
  LED led_4 (.in(CROM[13]));
  LED led_5 (.in(CROM[12]));
  // Probe on cond
  // Probe on CROM[10:9]
  LED led_6 (.in(CROM[11]));
  // Probe on addrsel
  LED led_7 (.in(CROM[6]));
  Clock clock_1 (.out(CLK));
  // Probe on DROM[7:0]
  Multiplexer #(.width(8)) multiplexer_1 (
    .in0(DROM[7:0]), .in1(DROM[15:8]), .out(multiplexer_1_out), .sel(multiplexer_2_out));
  // Probe on DROM[15:8]
  Multiplexer #(.select(2)) multiplexer_2 (
    .in0(Flags), .in1(or_1_out), .in2(in_3), .in3(opcode), .out(multiplexer_2_out), .sel(cond));
  Multiplexer #(.width(8)) multiplexer_3 (.in0({8{1'b0}}), .in1({1'b0, in_5}), .out(multiplexer_3_out), .sel(in_6));
  // Probe on DROM
  // Probe on CROM[5:4]
  // Probe on out_8
  Adder adder_1 (.a(multiplexer_1_out), .b(multiplexer_3_out), .out(out_8));  // open: cin, cout
  // Probe on aluop
  Button u_Reset (.out(reset));
  // Probe on out_8

  assign out_7 = Mikro_PC;

  // Other names for the same wires on the sheet: opcode_t[6:0] = in_5; c = Flags;
  //   CROM (some bits) = {in_6, cond, addrsel, aluop}; op2sel[1:0] = CROM[5:4]; datawrite = CROM[6];
  //   pcsel[1:0] = CROM[10:9]; pcload = CROM[11]; dwrite = CROM[12]; irload = CROM[13]; imload = CROM[14];
  //   regsrc[1:0] = CROM[16:15]; indexsel = in_6; datasel[1:0] = CROM[21:20]; swrite = CROM[22];
  //   MicroPC[7:0] = Mikro_PC; n = opcode; z = in_3

  // Notes on the sheet:
  //   Based on: http://minnie.tuhs.org/Programs/UcodeCPU/index.html
  //   v05: Migration to EVO, Debug, Counters, ImmReg Units
  //   Control ROM
  //   Address of third uinstruction is "opcode+2"
  //   contents of rom_1 (hex, n*v repeats v):
  //   2000 80800 11000 39*0 4000 22*0 1000 0 4000 62*0 40021 1000c0 800 a00
  //   contents of rom_2 (hex, n*v repeats v):
  //   101 202 40*0 8282 22*0 8484 0 8383 62*0 8485 8484
  //   Microcode Control Unit
  //   Decision ROM
  //   Micro Instruction
  //   Next uPC
  //   Quick tips:
  //   2a [42]:addrsel=pc  imload=1   # JNEZ Rs,immed
  //   84 [132]:   pcincr: pcload=1  pcsel=pc, goto fetch
  //   41 [65]:addrsel=pc  dwrite=1  regsrc=databus  # Load immediate Rd, immed
  //   43 [67]:addrsel=pc  imload=1    # Store Rd into address from immed
  //   82 [130]: aluop=sub  op2sel=const0, if z then pcincr else jump 
  //   85 [133]:   jump:  pcload=1  pcsel=immed, goto fetch
  //   Use ctrl+t to manually toggle global clock signal
  //   Use Simulate->Ticks Enabled for automatic clock signal
  //   2:aluop=add  op2sel=treg  dwrite=1  regsrc=aluout, goto fetch  # ALU operations on Rd,Rs,Rt
endmodule
