// Logisim project mimo_v04b_IR_Demo.circ as structural Verilog: 2 circuits, main circuit MiMo_v04b_OR
// address
module MiMo_v04b_OR (
  input  [15:0] instruction,
  input  irload,
  output [2:0] dregsel,
  output [2:0] sregsel,
  output [2:0] tregsel,
  output [6:0] opcode,
  output [15:0] Instruction_register
);

  wire CLK, reset;

  Register #(.width(16)) IR (
    .D(instruction), .en(irload), .Q({Instruction_register[15:3], dregsel}), .clk(CLK), .clr(reset));
  // Probe on {Instruction_register[15:3], dregsel}
  // Probe on dregsel
  // Probe on Instruction_register[5:3]
  // Probe on Instruction_register[8:6]
  // Probe on Instruction_register[15:9]
  Clock clock_1 (.out(CLK));
  Button u_Reset (.out(reset));

  assign Instruction_register[2:0] = dregsel;
  assign opcode = Instruction_register[15:9];
  assign sregsel = Instruction_register[5:3];
  assign tregsel = Instruction_register[8:6];

  // Notes on the sheet:
  //   IR Logic
  //   Zbirnik:  add Rd,Rs,Rt
  //   MiMo - Microprogrammed CPU Model
  //   FORMAT 1: Op.koda(7b) Treg(3b) Sreg(3b) Dreg(3b)
  //   v0.5
  //   OR
endmodule

module ShowHexa (
  input  [15:0] Data,
  output [3:0] out_2,
  output [3:0] out_3,
  output [3:0] out_4,
  output [3:0] Digit
);


  assign Digit = Data[3:0];
  assign out_2 = Data[15:12];
  assign out_3 = Data[11:8];
  assign out_4 = Data[7:4];
endmodule
