// Logisim project mimo_v04b_PC_Demo.circ as structural Verilog: 2 circuits, main circuit MiMo_v04b_OR
// address
module MiMo_v04b_OR (
  input  [15:0] imreg,
  input  [15:0] sreg,
  input  pcload,
  input  [1:0] pcsel,
  output [15:0] pcout
);

  wire CLK, reset;
  wire [15:0] adder_1_out, adder_2_out, multiplexer_1_out;

  // Probe on pcout
  // Probe on imreg
  // Probe on sreg
  Adder #(.width(16)) adder_1 (.a(pcout), .b(16'h1), .out(adder_1_out));  // open: cin, cout
  Adder #(.width(16)) adder_2 (.a(pcout), .b(imreg), .out(adder_2_out));  // open: cin, cout
  // Probe on pcsel
  // Probe on multiplexer_1_out
  Multiplexer #(.select(2), .width(16)) multiplexer_1 (
    .in0(adder_1_out), .in1(imreg), .in2(adder_2_out), .in3(sreg), .out(multiplexer_1_out), .sel(pcsel));
  Register #(.width(16)) PC (.D(multiplexer_1_out), .en(pcload), .Q(pcout), .clk(CLK), .clr(reset));
  // Probe on pcout
  Clock clock_1 (.out(CLK));
  // Probe on nothing
  Button u_Reset (.out(reset));

  // Notes on the sheet:
  //   PC=PC+1
  //   PC=immed
  //   PC=PC+immed
  //   PC=sreg
  //   MiMo - Microprogrammed CPU Model
  //   PC Logic
  //   v0.5
  //   OR
endmodule

module ShowHexa (
  input  [15:0] Data,
  output [3:0] Digit,
  output [3:0] out_3,
  output [3:0] out_4,
  output [3:0] out_5
);


  assign Digit = Data[15:12];
  assign out_3 = Data[11:8];
  assign out_4 = Data[7:4];
  assign out_5 = Data[3:0];
endmodule
