// Logisim project mimo_v04b_TTY_Demo.circ as structural Verilog: 2 circuits, main circuit MiMo_v04b_OR
// address
module MiMo_v04b_OR (
  input  [15:0] data,
  input  Write_Enable
);

  wire Clear_out, CLK, reset;

  // Probe on data[6:0]
  TTY #(.cols(16), .rows(4)) tty_1 (.data(data[6:0]), .clk(CLK), .we(Write_Enable), .clr(Clear_out));
  Button Clear (.out(Clear_out));
  Clock clock_1 (.out(CLK));
  Button u_Reset (.out(reset));

  // Notes on the sheet:
  //   MiMo - Microprogrammed CPU Model
  //   TTY
  //   v0.5
  //   OR
endmodule

module ShowHexa (
  input  [15:0] Data,
  output [3:0] out_2,
  output [3:0] Digit,
  output [3:0] out_4,
  output [3:0] out_5
);


  assign Digit = Data[11:8];
  assign out_2 = Data[15:12];
  assign out_4 = Data[7:4];
  assign out_5 = Data[3:0];
endmodule
