// Logisim project mimo_v04b_immed_Demo.circ as structural Verilog: 3 circuits, main circuit MiMo_v04b_OR
// address
module MiMo_v04b_OR (
  input  [15:0] in_1,
  input  imload,
  output [15:0] out_3
);

  wire CLK, reset;

  // Probe on in_1
  // Probe on out_3
  // ImmediateReg immediatereg_1: pin names not known; wires that end beside it: in_1, imload, CLK
  // Probe on out_3
  Clock clock_1 (.out(CLK));
  Button u_Reset (.out(reset));

  // Other names for the same wires on the sheet: immed[15:0] = out_3; sreg[15:0] = in_1

  // Notes on the sheet:
  //   Data Bus
  //   MiMo - Microprogrammed CPU Model
  //   Imm. Reg.
  //   v0.5
  //   OR
  //   immed
endmodule

module ShowHexa (
  input  [15:0] Data,
  output [3:0] out_2,
  output [3:0] out_3,
  output [3:0] Digit,
  output [3:0] out_5
);


  assign Digit = Data[7:4];
  assign out_2 = Data[15:12];
  assign out_3 = Data[11:8];
  assign out_5 = Data[3:0];
endmodule

module ImmediateReg (
  input  [15:0] DataIn,
  input  IMLoad,
  input  CLKin,
  output [15:0] ImmOut
);

  Register #(.width(16)) register_1 (.D(DataIn), .en(IMLoad), .Q(ImmOut), .clk(CLKin));  // open: clr
  // Probe on ImmOut
endmodule
