// Logisim project mimo_v05_Debug_Demo.circ as structural Verilog: 1 circuit, main circuit main
module main (
  input  [15:0] pcreg,
  input  [15:0] break_addr,
  input  break_on_addr,
  input  [7:0] ucounter,
  input  break_on_instr,
  input  break_on_cycle,
  output clock_out
);

  wire and_1_out, and_2_out, and_3_out, CLK_out, Continue_out, nor_1_out, nor_2_out, nor_3_out, or_1_out,
       Reset_out, shift_register_1_out, shift_register_1_q0;
  wire [15:0] xor_1_out;

  Button Reset (.out(Reset_out));
  Button Continue (.out(Continue_out));
  Clock CLK (.out(CLK_out));
  Shift_Register #(.length(2), .trigger("falling")) shift_register_1 (
    .in(Continue_out), .clk(CLK_out), .out(shift_register_1_out), .clr(Reset_out), .q0(shift_register_1_q0));  // open: shift, load, d0, d1, q1
  assign xor_1_out = pcreg ^ break_addr;  // XOR_Gate xor_1, 16 bits wide
  LED Addr (.in(break_on_addr));
  and and_1 (and_1_out, ~shift_register_1_out, shift_register_1_q0);  // AND_Gate
  nor nor_1 (nor_1_out, xor_1_out[15], xor_1_out[14], xor_1_out[13], xor_1_out[12], xor_1_out[11], xor_1_out[10], xor_1_out[9], xor_1_out[8], xor_1_out[6], xor_1_out[5], xor_1_out[4], xor_1_out[3], xor_1_out[2], xor_1_out[1], xor_1_out[0], xor_1_out[7]);
  and and_2 (and_2_out, nor_1_out, break_on_addr, nor_2_out);
  nor nor_2 (nor_2_out, ucounter[7], ucounter[6], ucounter[5], ucounter[4], ucounter[2], ucounter[1], ucounter[0], ucounter[3]);
  and and_3 (and_3_out, nor_2_out, break_on_instr);
  LED Instr (.in(break_on_instr));
  LED Cycle (.in(break_on_cycle));
  nor nor_3 (nor_3_out, and_2_out, and_3_out, break_on_cycle);
  or or_1 (or_1_out, and_1_out, nor_3_out);
  LED Pass (.in(or_1_out));
  and and_4 (clock_out, CLK_out, or_1_out);

  // Notes on the sheet:
  //   Breaks on PC = break_addr
  //   Breaks on each new instruction
  //   Breaks on each clock pulse
  //   Makes sure the 'continue' button only
  //   lets through 1 clock pulse, until you let go
  //   and press it again.
  //   Outputs 1 only on first cycle (shift bits are unequal).
  //   Debug Unit
  //   PC = break_addr?
endmodule
