// Logisim project mimo_v03c.circ as structural Verilog: 5 circuits, main circuit main
// address
module main (
  input  Reset,
  output [7:0] ucounter
);

  wire c, Clock_2_out, Clock_3_out, Clock_4_out, Clock_5_out, Clock_out, datawrite, dwrite, imload, indexsel,
       irload, multiplexer_4_out, n, Ncmd, not_1_out, or_1_out, or_2_out, pcload, swrite, twrite, z;
  wire [1:0] addrsel, cond, datasel, op2sel, pcsel, regsrc;
  wire [2:0] dregs, sregs, tregs;
  wire [3:0] aluop, icycles;
  wire [6:0] opcode;
  wire [7:0] adder_1_out, multiplexer_3_out, multiplexer_5_out;
  wire [15:0] address, aluout, cycles, data, dreg, immed, irreg, multiplexer_2_out, multiplexer_6_out,
       multiplexer_7_out, pc, ram_1_data, registerfile_1_r0, registerfile_1_r1, registerfile_1_r2,
       registerfile_1_r3, registerfile_1_r4, registerfile_1_r5, registerfile_1_r6, registerfile_1_r7,
       rom_2_data, sreg, treg;
  wire [31:23] rom_1_data;

  // Probe on swrite
  Hex_Digit_Display hex_digit_display_1 (.value(address[11:8]));  // open: dp
  Hex_Digit_Display hex_digit_display_2 (.value(address[15:12]));  // open: dp
  // Probe on ucounter
  nor nor_1 (Ncmd, ucounter[0], ucounter[1], ucounter[2], ucounter[3], ucounter[5], ucounter[6], ucounter[7], ucounter[4]);
  // Probe on indexsel
  // Probe on datasel
  Hex_Digit_Display hex_digit_display_3 (.value(address[7:4]));  // open: dp
  Clock Clock (.out(Clock_out));
  Register Microcounter (.D(adder_1_out), .Q(ucounter), .clk(Clock_2_out), .clr(Reset));  // open: en
  Clock Clock_2 (.out(Clock_2_out));
  // Probe on cond
  // Probe on regsrc
  // Probe on address
  Hex_Digit_Display hex_digit_display_4 (.value(address[3:0]));  // open: dp
  Hex_Digit_Display hex_digit_display_5 (.value(ram_1_data[15:12]));  // open: dp
  RAM #(.addrWidth(16), .dataWidth(16)) ram_1 (
    .addr(address), .data(ram_1_data), .sel(1'b1), .clk(Clock_out), .ld(not_1_out));  // open: clr
  not not_1 (not_1_out, datawrite);
  // Probe on irload
  // Probe on imload
  Hex_Digit_Display hex_digit_display_6 (.value(ram_1_data[11:8]));  // open: dp
  Hex_Digit_Display hex_digit_display_7 (.value(ram_1_data[7:4]));  // open: dp
  ROM #(.dataWidth(32)) rom_1 (
    .addr(ucounter),
    .data({rom_1_data, swrite, datasel, indexsel, cond, regsrc, imload, irload, dwrite, pcload, pcsel, addrsel, datawrite, op2sel, aluop}));  // open: sel
  ROM #(.dataWidth(16)) rom_2 (.addr(ucounter), .data(rom_2_data));  // open: sel
  // Probe on opcode
  // Probe on dwrite
  // Probe on pcload
  Multiplexer #(.select(2), .width(16), .enable("false")) multiplexer_1 (
    .in0(pc), .in1(immed), .in2(aluout), .in3(sreg), .out(address), .sel(addrsel));
  // Probe on addrsel
  Hex_Digit_Display hex_digit_display_8 (.value(ram_1_data[3:0]));  // open: dp
  // Probe on ram_1_data
  or or_1 (or_1_out, c, z);
  // Probe on cond
  // Probe on addrsel
  // Probe on pcsel
  assign ram_1_data = datawrite ? multiplexer_2_out : 16'bz;  // Controlled_Buffer controlled_buffer_1
  Multiplexer #(.select(2), .width(16), .enable("false")) multiplexer_2 (
    .in0(pc), .in1(dreg), .in2(treg), .in3(aluout), .out(multiplexer_2_out), .sel(datasel));
  // Probe on datasel
  // Probe on rom_2_data[7:0]
  Multiplexer #(.width(8), .enable("false")) multiplexer_3 (
    .in0(rom_2_data[7:0]), .in1(rom_2_data[15:8]), .out(multiplexer_3_out), .sel(multiplexer_4_out));
  // Probe on rom_2_data[15:8]
  Multiplexer #(.select(2), .enable("false")) multiplexer_4 (
    .in0(c), .in1(or_1_out), .in2(z), .in3(n), .out(multiplexer_4_out), .sel(cond));
  Multiplexer #(.width(8), .enable("false")) multiplexer_5 (
    .in0({8{1'b0}}), .in1({1'b0, opcode}), .out(multiplexer_5_out), .sel(indexsel));
  // Probe on datawrite
  // Probe on op2sel
  Register #(.width(16)) IMM (.D(ram_1_data), .en(imload), .Q(immed), .clk(Clock_3_out));  // open: clr
  // Probe on immed
  Clock Clock_3 (.out(Clock_3_out));
  // Probe on adder_1_out
  Adder adder_1 (.a(multiplexer_3_out), .b(multiplexer_5_out), .out(adder_1_out));  // open: cin, cout
  // Probe on aluop
  // Probe on pc
  PC_logic pc_logic_1 (.imreg(immed), .sreg(sreg), .pcout(pc), .pcsel(pcsel), .pcload(pcload), .reset(Reset));
  // Probe on tregs
  // Probe on opcode
  Multiplexer #(.select(2), .width(16), .enable("false")) multiplexer_6 (
    .in0(ram_1_data), .in1(immed), .in2(aluout), .in3(sreg), .out(multiplexer_6_out), .sel(regsrc));
  // Probe on multiplexer_6_out
  // Probe on regsrc
  instruction_register instruction_register_1 (
    .instruction(ram_1_data), .irload(irload), .dregsel(dregs), .sregsel(sregs), .tregsel(tregs),
    .opcode(opcode), .Instruction_register(irreg), .reset(Reset));
  // Probe on irreg
  // Probe on dregs
  // Probe on sregs
  registerfile registerfile_1 (
    .dwrite(dwrite), .regval(multiplexer_6_out), .sreg(sreg), .treg(treg), .dsel(dregs), .ssel(sregs),
    .tsel(tregs), .r0(registerfile_1_r0), .r1(registerfile_1_r1), .r2(registerfile_1_r2),
    .r7(registerfile_1_r7), .r6(registerfile_1_r6), .r5(registerfile_1_r5), .r4(registerfile_1_r4),
    .r3(registerfile_1_r3), .twrite(twrite), .dreg(dreg), .swrite(swrite), .Reset(Reset));
  // Probe on opcode
  Counter #(.width(16), .max('hffff), .ongoal("stay")) Cycles_Cnt (
    .Q(cycles), .clk(Clock_4_out), .clr(Reset));  // open: load, D, count, carry
  Clock Clock_4 (.out(Clock_4_out));
  LED New_CMD (.in(Ncmd));
  // Probe on address
  // Probe on registerfile_1_r0
  // Probe on registerfile_1_r1
  // Probe on registerfile_1_r2
  // Probe on registerfile_1_r3
  // Probe on registerfile_1_r4
  // Probe on registerfile_1_r5
  // Probe on registerfile_1_r6
  // Probe on registerfile_1_r7
  // Probe on dregs
  // Probe on sregs
  // Probe on tregs
  Clock Clock_5 (.out(Clock_5_out));
  // Probe on data
  // Probe on pc
  // Probe on irreg
  // Probe on immed
  // Probe on aluout
  // Probe on dreg
  // Probe on sreg
  // Probe on treg
  Multiplexer #(.select(2), .width(16), .enable("false")) multiplexer_7 (
    .in0(treg), .in1(immed), .in2({16{1'b0}}), .in3(16'h1), .out(multiplexer_7_out), .sel(op2sel));
  // Probe on op2sel
  Counter #(.width(4), .max('hf), .ongoal("stay")) Instr_Cycles_Cnt (
    .Q(icycles), .clk(Clock_5_out), .clr(or_2_out));  // open: load, D, count, carry
  or or_2 (or_2_out, Ncmd, Reset);
  // Probe on irreg
  LED u_C (.in(c));
  LED u_Z (.in(z));
  LED u_N (.in(n));
  ALU alu_2 (.Zero(z), .Negative(n), .Result(aluout), .aluop(aluop), .A(sreg), .B(multiplexer_7_out), .Carry(c));
  // Probe on sreg
  // Probe on multiplexer_7_out
  // Probe on aluop
  // Probe on icycles
  // Probe on aluout
  // Probe on cycles

  // Notes on the sheet:
  //   Address BUS
  //   RAM
  //   Microcode Control Unit
  //   Control ROM
  //   Address of first uinstruction is "opcode+2"
  //   MiMo - Microprogrammed CPU Model
  //   Microinstruction
  //   Data BUS
  //   contents of rom_1 (hex, n*v repeats v):
  //   2000 80800 11000 39*0 4000 22*0 1000 0 4000 62*0 40021 1000c0 800 a00
  //   Decision ROM
  //   contents of rom_2 (hex, n*v repeats v):
  //   101 202 40*0 8282 22*0 8484 0 8383 62*0 8485 8484
  //   Immed. Reg.
  //   v03c
  //   PC
  //   Ins.Reg.
  //   Based on: http://minnie.tuhs.org/Programs/UcodeCPU/index.html
  //   v03b: Fix z cond code
  //   v03a: Basic functionality, Microcode logic on main
  //   Quick tips:
  //   2a [42]:	addrsel=pc  imload=1   # JNEZ Rs,immed
  //   43 [67]:	addrsel=pc  imload=1    # Store Rd into address from immed
  //   84 [132]:   pcincr:	 pcload=1  pcsel=pc, goto fetch
  //   85 [133]:   jump:	  pcload=1  pcsel=immed, goto fetch
  //   Registers
  //   2:	aluop=add  op2sel=treg  dwrite=1  regsrc=aluout, goto fetch  # ALU operations on Rd,Rs,Rt
  //   41 [65]:	addrsel=pc  dwrite=1  regsrc=databus  # Load immediate Rd, immed
  //   Use ctrl+t to manually toggle global clock signal
  //   Use Simulate->Ticks Enabled for automatic clock signal
  //   Status
  //   ALU
endmodule

module instruction_register (
  input  [15:0] instruction,
  input  reset,
  input  irload,
  output [2:0] dregsel,
  output [2:0] sregsel,
  output [2:0] tregsel,
  output [6:0] opcode,
  output [15:0] Instruction_register
);

  wire Clock_out;

  Clock Clock (.out(Clock_out));
  Register #(.width(16)) IR (
    .D(instruction), .en(irload), .Q({Instruction_register[15:3], dregsel}), .clk(Clock_out), .clr(reset));

  assign Instruction_register[2:0] = dregsel;
  assign opcode = Instruction_register[15:9];
  assign sregsel = Instruction_register[5:3];
  assign tregsel = Instruction_register[8:6];

  // Notes on the sheet:
  //   IR Logic
endmodule

module registerfile (
  input  [15:0] regval,
  input  Reset,
  input  dwrite,
  input  swrite,
  input  twrite,
  input  [2:0] dsel,
  input  [2:0] ssel,
  input  [2:0] tsel,
  output [15:0] r0,
  output [15:0] r1,
  output [15:0] r2,
  output [15:0] r3,
  output [15:0] r4,
  output [15:0] r5,
  output [15:0] r6,
  output [15:0] r7,
  output [15:0] dreg,
  output [15:0] sreg,
  output [15:0] treg
);

  wire Clock_out, demultiplexer_1_out0, demultiplexer_1_out1, demultiplexer_1_out2, demultiplexer_1_out3,
       demultiplexer_1_out4, demultiplexer_1_out5, demultiplexer_1_out6, demultiplexer_1_out7;

  Demultiplexer #(.select(3), .enable("false")) demultiplexer_1 (
    .out0(demultiplexer_1_out0), .out1(demultiplexer_1_out1), .out2(demultiplexer_1_out2),
    .out3(demultiplexer_1_out3), .out4(demultiplexer_1_out4), .out5(demultiplexer_1_out5),
    .out6(demultiplexer_1_out6), .out7(demultiplexer_1_out7), .in(dwrite), .sel(dsel));
  Demultiplexer #(.select(3), .enable("false")) demultiplexer_2 (
    .out0(demultiplexer_1_out0), .out1(demultiplexer_1_out1), .out2(demultiplexer_1_out2),
    .out3(demultiplexer_1_out3), .out4(demultiplexer_1_out4), .out5(demultiplexer_1_out5),
    .out6(demultiplexer_1_out6), .out7(demultiplexer_1_out7), .in(swrite), .sel(ssel));
  Demultiplexer #(.select(3), .enable("false")) demultiplexer_3 (
    .out0(demultiplexer_1_out0), .out1(demultiplexer_1_out1), .out2(demultiplexer_1_out2),
    .out3(demultiplexer_1_out3), .out4(demultiplexer_1_out4), .out5(demultiplexer_1_out5),
    .out6(demultiplexer_1_out6), .out7(demultiplexer_1_out7), .in(twrite), .sel(tsel));
  Register #(.width(16)) register_1 (.D(regval), .en(demultiplexer_1_out0), .Q(r0), .clk(Clock_out), .clr(Reset));
  Register #(.width(16)) register_2 (.D(regval), .en(demultiplexer_1_out1), .Q(r1), .clk(Clock_out), .clr(Reset));
  Register #(.width(16)) register_3 (.D(regval), .en(demultiplexer_1_out2), .Q(r2), .clk(Clock_out), .clr(Reset));
  Register #(.width(16)) register_4 (.D(regval), .en(demultiplexer_1_out3), .Q(r3), .clk(Clock_out), .clr(Reset));
  Register #(.width(16)) register_5 (.D(regval), .en(demultiplexer_1_out4), .Q(r4), .clk(Clock_out), .clr(Reset));
  Register #(.width(16)) register_6 (.D(regval), .en(demultiplexer_1_out5), .Q(r5), .clk(Clock_out), .clr(Reset));
  Register #(.width(16)) register_7 (.D(regval), .en(demultiplexer_1_out6), .Q(r6), .clk(Clock_out), .clr(Reset));
  Register #(.width(16)) register_8 (.D(regval), .en(demultiplexer_1_out7), .Q(r7), .clk(Clock_out), .clr(Reset));
  Clock Clock (.out(Clock_out));
  Multiplexer #(.select(3), .width(16), .enable("false")) multiplexer_1 (
    .in0(r0), .in1(r1), .in2(r2), .in3(r3), .in4(r4), .in5(r5), .in6(r6), .in7(r7), .out(dreg), .sel(dsel));
  Multiplexer #(.select(3), .width(16), .enable("false")) multiplexer_2 (
    .in0(r0), .in1(r1), .in2(r2), .in3(r3), .in4(r4), .in5(r5), .in6(r6), .in7(r7), .out(sreg), .sel(ssel));
  Multiplexer #(.select(3), .width(16), .enable("false")) multiplexer_3 (
    .in0(r0), .in1(r1), .in2(r2), .in3(r3), .in4(r4), .in5(r5), .in6(r6), .in7(r7), .out(treg), .sel(tsel));

  // Notes on the sheet:
  //   Register File
endmodule

module ALU (
  input  [15:0] A,
  input  [15:0] B,
  input  [3:0] aluop,
  output Carry,
  output Zero,
  output Negative,
  output [15:0] Result
);

  wire adder_1_cout, or_2_out, subtractor_1_bout;
  wire [15:0] adder_1_out, and_1_out, divider_1_out, divider_1_rem, multiplier_1_out, nand_1_out, nor_1_out,
       not_1_out, or_1_out, shifter_1_out, shifter_2_out, shifter_3_out, shifter_4_out, shifter_5_out,
       subtractor_1_out, xor_1_out;

  Adder #(.width(16)) adder_1 (.a(A), .b(B), .out(adder_1_out), .cin(1'b0), .cout(adder_1_cout));
  Subtractor #(.width(16)) subtractor_1 (.a(A), .b(B), .out(subtractor_1_out), .bin(1'b0), .bout(subtractor_1_bout));
  Multiplier #(.width(16)) multiplier_1 (.a(A), .b(B), .out(multiplier_1_out), .cin({16{1'b0}}));  // open: cout
  Divider #(.width(16)) divider_1 (.a(A), .b(B), .out(divider_1_out), .upper({16{1'b0}}), .rem(divider_1_rem));
  assign and_1_out = A & B;  // AND_Gate and_1, 16 bits wide
  assign or_1_out = A | B;  // OR_Gate or_1, 16 bits wide
  assign xor_1_out = A ^ B;  // XOR_Gate xor_1, 16 bits wide
  assign nand_1_out = ~(A & B);  // NAND_Gate nand_1, 16 bits wide
  assign nor_1_out = ~(A | B);  // NOR_Gate nor_1, 16 bits wide
  assign not_1_out = ~A;  // NOT_Gate not_1, 16 bits wide
  Shifter #(.width(16)) shifter_1 (.in(A), .\dist (B[3:0]), .out(shifter_1_out));
  Shifter #(.width(16), .shift("lr")) shifter_2 (.in(A), .\dist (B[3:0]), .out(shifter_2_out));
  Shifter #(.width(16), .shift("ar")) shifter_3 (.in(A), .\dist (B[3:0]), .out(shifter_3_out));
  Shifter #(.width(16), .shift("rl")) shifter_4 (.in(A), .\dist (B[3:0]), .out(shifter_4_out));
  Shifter #(.width(16), .shift("rr")) shifter_5 (.in(A), .\dist (B[3:0]), .out(shifter_5_out));
  Multiplexer #(.select(4), .width(16), .enable("false")) multiplexer_1 (
    .in0(adder_1_out), .in1(subtractor_1_out), .in2(multiplier_1_out), .in3(divider_1_out),
    .in4(divider_1_rem), .in5(and_1_out), .in6(or_1_out), .in7(xor_1_out), .in8(nand_1_out), .in9(nor_1_out),
    .in10(not_1_out), .in11(shifter_1_out), .in12(shifter_2_out), .in13(shifter_3_out), .in14(shifter_4_out),
    .in15(shifter_5_out), .out({Negative, Result[14:0]}), .sel(aluop));
  Multiplexer #(.select(4), .enable("false")) multiplexer_2 (
    .in0(adder_1_cout), .in1(subtractor_1_bout), .in2(1'b0), .in3(1'b0), .in4(1'b0), .in5(1'b0), .in6(1'b0),
    .in7(1'b0), .in8(1'b0), .in9(1'b0), .in10(1'b0), .in11(1'b0), .in12(1'b0), .in13(1'b0), .in14(1'b0),
    .in15(1'b0), .out(Carry), .sel(aluop));
  not not_2 (Zero, or_2_out);
  or or_2 (or_2_out, Result[0], Result[1], Result[2], Result[3], Result[4], Result[5], Result[6], Result[7], Result[9], Result[10], Result[11], Result[12], Result[13], Result[14], Negative, Result[8]);

  assign Result[15] = Negative;

  // Notes on the sheet:
  //   16-bit ALU
endmodule

module PC_logic (
  input  [15:0] imreg,
  input  pcload,
  input  reset,
  input  [15:0] sreg,
  input  [1:0] pcsel,
  output [15:0] pcout
);

  wire Clock_out;
  wire [15:0] adder_1_out, adder_2_out, multiplexer_1_out;

  Adder #(.width(16)) adder_1 (.a(pcout), .b(16'h1), .out(adder_1_out));  // open: cin, cout
  Adder #(.width(16)) adder_2 (.a(pcout), .b(imreg), .out(adder_2_out));  // open: cin, cout
  Multiplexer #(.select(2), .width(16), .enable("false")) multiplexer_1 (
    .in0(adder_1_out), .in1(imreg), .in2(adder_2_out), .in3(sreg), .out(multiplexer_1_out), .sel(pcsel));
  Register #(.width(16)) PC (.D(multiplexer_1_out), .en(pcload), .Q(pcout), .clk(Clock_out), .clr(reset));
  Clock Clock (.out(Clock_out));

  // Notes on the sheet:
  //   PC Logic
endmodule
