// Logisim project mimo_v05a_HardWired_EVO.circ as structural Verilog: 12 circuits, main circuit MiMo_v05
// address
module MiMo_v05 (
  input  Cycle,
  input  Stop,
  input  Instr,
  input  [15:0] Addr
);

  wire ADDR_DEC_output_3, and_1_out, and_2_out, and_3_out, and_4_out, c, Clear_out, Clear_Screen_out, CLK,
       CLKIN, cont, datawrite, dwrite, FB_LED, imload, indexsel, irload, n, Ncmd, not_1_out, pcload, RAMSel,
       reset, swrite, TTYSel, twrite, z;
  wire [1:0] addrsel, cond, datasel, op2sel, pcsel, Phase, regsrc;
  wire [2:0] dregs, sregs, tregs;
  wire [3:0] aluop, icycles, showhexa_1_digit, showhexa_1_out_2, showhexa_1_out_3, showhexa_1_out_5,
       showhexa_2_digit, showhexa_2_out_2, showhexa_2_out_3, showhexa_2_out_5;
  wire [6:0] opcode;
  wire [15:0] address, aluout, cmds, cycles, data, dreg, frame_buffer_16x16_1_out_6,
       frame_buffer_16x16_1_out_7, frame_buffer_16x16_1_out_8, frame_buffer_16x16_1_out_9,
       frame_buffer_16x16_1_out_10, frame_buffer_16x16_1_out_11, frame_buffer_16x16_1_out_12,
       frame_buffer_16x16_1_out_13, frame_buffer_16x16_1_out_14, frame_buffer_16x16_1_out_15,
       frame_buffer_16x16_1_out_16, frame_buffer_16x16_1_out_17, frame_buffer_16x16_1_out_18,
       frame_buffer_16x16_1_out_19, frame_buffer_16x16_1_out_20, frame_buffer_16x16_1_out_21, immed, irreg,
       multiplexer_2_out, multiplexer_3_out, multiplexer_4_out, pcreg, registerfile_1_r0, registerfile_1_r1,
       registerfile_1_r2, registerfile_1_r3, registerfile_1_r4, registerfile_1_r5, registerfile_1_r6,
       registerfile_1_r7, sreg, treg;

  Hex_Digit_Display hex_digit_display_1 (.value(showhexa_1_out_2));  // open: dp
  ShowHexa showhexa_1 (
    .Data(address), .Digit(showhexa_1_digit), .out_5(showhexa_1_out_5), .out_2(showhexa_1_out_2),
    .out_3(showhexa_1_out_3));
  RAM #(.addrWidth(14), .asyncread("true"), .dataWidth(16), .databus("bidir")) ram_1 (
    .addr(address[13:0]), .we(and_2_out), .oe(and_1_out), .clk(CLK), .data(data));
  Hex_Digit_Display hex_digit_display_2 (.value(showhexa_1_digit));  // open: dp
  Hex_Digit_Display hex_digit_display_3 (.value(showhexa_1_out_3));  // open: dp
  and and_1 (and_1_out, RAMSel, not_1_out);
  not not_1 (not_1_out, datawrite);
  and and_2 (and_2_out, RAMSel, datawrite);
  Address_Decoder ADDR_DEC (
    .Address(address), .RAM(RAMSel), .FB_LED(FB_LED), .TTY(TTYSel), .output_3(ADDR_DEC_output_3));  // open: in_2, in_3
  Clock SysClk (.out(CLKIN));
  Hex_Digit_Display hex_digit_display_4 (.value(showhexa_1_out_5));  // open: dp
  Hex_Digit_Display hex_digit_display_5 (.value(showhexa_2_out_2));  // open: dp
  ShowHexa showhexa_2 (
    .Data(data), .Digit(showhexa_2_digit), .out_5(showhexa_2_out_5), .out_2(showhexa_2_out_2),
    .out_3(showhexa_2_out_3));
  // Probe on address
  Multiplexer #(.select(2), .width(16)) multiplexer_1 (
    .in0(pcreg), .in1(immed), .in2(aluout), .in3(sreg), .out(address), .sel(addrsel));
  Hex_Digit_Display hex_digit_display_6 (.value(showhexa_2_out_3));  // open: dp
  Hex_Digit_Display hex_digit_display_7 (.value(showhexa_2_digit));  // open: dp
  assign data = datawrite ? multiplexer_2_out : 16'bz;  // Controlled_Buffer controlled_buffer_1
  Multiplexer #(.select(2), .width(16)) multiplexer_2 (
    .in0(pcreg), .in1(dreg), .in2(treg), .in3(aluout), .out(multiplexer_2_out), .sel(datasel));
  // Probe on datasel
  ControlUnit_HW controlunit_hw_1 (
    .opcode(opcode), .c(c), .z(z), .n(n), .clock(CLK), .phase(Phase), .swrite(swrite), .irload(irload),
    .imload(imload), .dwrite(dwrite), .regsrc(regsrc), .datawrite(datawrite), .addrsel(addrsel),
    .aluop(aluop), .datasel(datasel), .pcload(pcload), .op2sel(op2sel), .pcsel(pcsel));
  Counters counters_1 (
    .new_ucounter(Phase), .reset(reset), .clock(CLK), .cmds(cmds), .cycles(cycles), .icycles(icycles));
  // Probe on addrsel
  Hex_Digit_Display hex_digit_display_8 (.value(showhexa_2_out_5));  // open: dp
  // Probe on data
  // Probe on pcreg
  PC pc_1 (.imreg(immed), .sreg(sreg), .pcsel(pcsel), .pcload(pcload), .clock(CLK), .reset(reset), .pcout(pcreg));
  // Probe on immed
  ImmediateReg immediatereg_1 (.IMLoad(imload), .CLKin(CLK), .DataIn(data), .ImmOut(immed));
  InstructionReg instructionreg_1 (
    .reset(reset), .irload(irload), .instruction(data), .clock(CLK), .dregsel(dregs), .sregsel(sregs),
    .tregsel(tregs), .opcode(opcode), .Instruction_register_Content(irreg));
  // Probe on irreg
  // Probe on opcode
  // Probe on multiplexer_3_out
  Multiplexer #(.select(2), .width(16)) multiplexer_3 (
    .in0(data), .in1(immed), .in2(aluout), .in3(sreg), .out(multiplexer_3_out), .sel(regsrc));
  // Probe on regsrc
  Button u_Reset (.out(reset));
  Registerfile registerfile_1 (
    .dsel(dregs), .regval(multiplexer_3_out), .dwrite(dwrite), .ssel(sregs), .swrite(swrite), .tsel(tregs),
    .twrite(twrite), .clock(CLK), .Reset(reset), .dreg(dreg), .sreg(sreg), .treg(treg),
    .r0(registerfile_1_r0), .r1(registerfile_1_r1), .r2(registerfile_1_r2), .r3(registerfile_1_r3),
    .r4(registerfile_1_r4), .r5(registerfile_1_r5), .r6(registerfile_1_r6), .r7(registerfile_1_r7));
  // Probe on sregs
  // Probe on dregs
  // Probe on Phase
  // Probe on datasel
  LED led_1 (.in(swrite));
  Frame_Buffer_16x16 frame_buffer_16x16_1 (
    .address(address[3:0]), .store(and_3_out), .data(data), .clock(CLK), .reset(Clear_out),
    .out_6(frame_buffer_16x16_1_out_6), .out_7(frame_buffer_16x16_1_out_7),
    .out_8(frame_buffer_16x16_1_out_8), .out_9(frame_buffer_16x16_1_out_9),
    .out_10(frame_buffer_16x16_1_out_10), .out_11(frame_buffer_16x16_1_out_11),
    .out_12(frame_buffer_16x16_1_out_12), .out_13(frame_buffer_16x16_1_out_13),
    .out_14(frame_buffer_16x16_1_out_14), .out_15(frame_buffer_16x16_1_out_15),
    .out_16(frame_buffer_16x16_1_out_16), .out_17(frame_buffer_16x16_1_out_17),
    .out_18(frame_buffer_16x16_1_out_18), .out_19(frame_buffer_16x16_1_out_19),
    .out_20(frame_buffer_16x16_1_out_20), .out_21(frame_buffer_16x16_1_out_21));
  and and_3 (and_3_out, FB_LED, datawrite);
  // Probe on registerfile_1_r0
  // Probe on registerfile_1_r1
  // Probe on registerfile_1_r2
  // Probe on registerfile_1_r3
  // Probe on registerfile_1_r4
  // Probe on registerfile_1_r5
  // Probe on registerfile_1_r6
  // Probe on registerfile_1_r7
  // Probe on dreg
  // Probe on sreg
  // Probe on treg
  // Probe on tregs
  LED led_2 (.in(indexsel));
  DotMatrix #(.inputtype("row"), .matrixcols(16), .matrixrows(16)) dotmatrix_1 (
    .row0(frame_buffer_16x16_1_out_21), .row1(frame_buffer_16x16_1_out_20),
    .row2(frame_buffer_16x16_1_out_19), .row3(frame_buffer_16x16_1_out_18),
    .row4(frame_buffer_16x16_1_out_17), .row5(frame_buffer_16x16_1_out_16),
    .row6(frame_buffer_16x16_1_out_15), .row7(frame_buffer_16x16_1_out_14),
    .row8(frame_buffer_16x16_1_out_13), .row9(frame_buffer_16x16_1_out_12),
    .row10(frame_buffer_16x16_1_out_11), .row11(frame_buffer_16x16_1_out_10),
    .row12(frame_buffer_16x16_1_out_9), .row13(frame_buffer_16x16_1_out_8),
    .row14(frame_buffer_16x16_1_out_7), .row15(frame_buffer_16x16_1_out_6));
  Button Clear (.out(Clear_out));
  Multiplexer #(.select(2), .width(16)) multiplexer_4 (
    .in0(treg), .in1(immed), .in2({16{1'b0}}), .in3(16'h1), .out(multiplexer_4_out), .sel(op2sel));
  // Probe on op2sel
  // Probe on cond
  // Probe on regsrc
  Button u_Cont (.out(cont));
  ALU alu_1 (.A(sreg), .B(multiplexer_4_out), .aluop(aluop), .Result(aluout), .Carry(c), .Zero(z), .Negative(n));
  // Probe on sreg
  // Probe on multiplexer_4_out
  // Probe on aluop
  LED led_3 (.in(irload));
  LED led_4 (.in(imload));
  DebugUnit debugunit_1 (
    .reset(reset), .\continue (cont), .clock(CLKIN), .pcreg(pcreg), .break_addr(Addr), .break_on_addr(Stop),
    .ucounter(Phase), .break_on_instr(Instr), .break_on_cycle(Cycle), .clock_out(CLK));
  // Probe on aluout
  // Probe on icycles
  LED led_5 (.in(dwrite));
  LED led_6 (.in(pcload));
  // Probe on opcode
  LED u_C (.in(c));
  LED u_Z (.in(z));
  LED u_N (.in(n));
  // Probe on cycles
  // Probe on pcsel
  // Probe on addrsel
  // Probe on data[6:0]
  TTY #(.cols(16), .rows(4)) tty_1 (.data(data[6:0]), .clk(CLK), .we(and_4_out), .clr(Clear_Screen_out));
  and and_4 (and_4_out, TTYSel, datawrite);
  // Probe on tregs
  // Probe on sregs
  // Probe on address
  // Probe on pcreg
  // Probe on irreg
  // Probe on immed
  // Probe on aluout
  LED New_CMD (.in(Ncmd));
  // Probe on op2sel
  LED led_7 (.in(datawrite));
  Button Clear_Screen (.out(Clear_Screen_out));
  // Probe on irreg
  // Probe on dregs
  // Probe on data
  // Probe on cmds
  // Probe on aluop

  // Other names for the same wires on the sheet: dbgadr = Stop; dbgcyc = Cycle; dbgins = Instr

  // Notes on the sheet:
  //   Address BUS
  //   Only 4 initial instructions execution supported !
  //   RAM
  //   MiMo - Microprogrammed CPU Model
  //   HardWired Control Unit
  //   Data BUS
  //   Based on: http://minnie.tuhs.org/Programs/UcodeCPU/index.html
  //   v05: Migration to EVO, Debug, Counters, ImmReg Units
  //   v0.5a EVO
  //   PC
  //   ImmReg
  //   InsReg
  //   Quick tips:
  //   Use ctrl+t to manually toggle global clock signal
  //   Registers
  //   Use Simulate->Ticks Enabled for automatic clock signal
  //   Debug
  //   Frame Buffer LED 16x16
  //   ALU
  //   Micro Instruction
  //   Instruction:
  //   Flags
  //   Status
  //   TTY
  //   Address, Data Bus
  //   Spec. Registers
endmodule

module InstructionReg (
  input  [15:0] instruction,
  input  reset,
  input  clock,
  input  irload,
  output [2:0] dregsel,
  output [2:0] sregsel,
  output [2:0] tregsel,
  output [6:0] opcode,
  output [15:0] Instruction_register_Content
);

  Register #(.width(16)) register_1 (
    .D(instruction), .en(irload), .Q({Instruction_register_Content[15:3], dregsel}), .clk(clock), .clr(reset));

  assign Instruction_register_Content[2:0] = dregsel;
  assign opcode = Instruction_register_Content[15:9];
  assign sregsel = Instruction_register_Content[5:3];
  assign tregsel = Instruction_register_Content[8:6];

  // Notes on the sheet:
  //   IR Logic
endmodule

module Registerfile (
  input  [15:0] regval,
  input  Reset,
  input  clock,
  input  dwrite,
  input  swrite,
  input  twrite,
  input  [2:0] dsel,
  input  [2:0] ssel,
  input  [2:0] tsel,
  output [15:0] r0,
  output [15:0] r1,
  output [15:0] r2,
  output [15:0] r3,
  output [15:0] r4,
  output [15:0] r5,
  output [15:0] r6,
  output [15:0] r7,
  output [15:0] dreg,
  output [15:0] sreg,
  output [15:0] treg
);

  wire demultiplexer_1_out0, demultiplexer_1_out1, demultiplexer_1_out2, demultiplexer_1_out3,
       demultiplexer_1_out4, demultiplexer_1_out5, demultiplexer_1_out6, demultiplexer_1_out7;

  Demultiplexer #(.select(3)) demultiplexer_1 (
    .out0(demultiplexer_1_out0), .out1(demultiplexer_1_out1), .out2(demultiplexer_1_out2),
    .out3(demultiplexer_1_out3), .out4(demultiplexer_1_out4), .out5(demultiplexer_1_out5),
    .out6(demultiplexer_1_out6), .out7(demultiplexer_1_out7), .in(dwrite), .sel(dsel));
  Demultiplexer #(.select(3)) demultiplexer_2 (
    .out0(demultiplexer_1_out0), .out1(demultiplexer_1_out1), .out2(demultiplexer_1_out2),
    .out3(demultiplexer_1_out3), .out4(demultiplexer_1_out4), .out5(demultiplexer_1_out5),
    .out6(demultiplexer_1_out6), .out7(demultiplexer_1_out7), .in(swrite), .sel(ssel));
  Demultiplexer #(.select(3)) demultiplexer_3 (
    .out0(demultiplexer_1_out0), .out1(demultiplexer_1_out1), .out2(demultiplexer_1_out2),
    .out3(demultiplexer_1_out3), .out4(demultiplexer_1_out4), .out5(demultiplexer_1_out5),
    .out6(demultiplexer_1_out6), .out7(demultiplexer_1_out7), .in(twrite), .sel(tsel));
  Register #(.width(16)) register_1 (.D(regval), .en(demultiplexer_1_out0), .Q(r0), .clk(clock), .clr(Reset));
  Register #(.width(16)) register_2 (.D(regval), .en(demultiplexer_1_out1), .Q(r1), .clk(clock), .clr(Reset));
  Register #(.width(16)) register_3 (.D(regval), .en(demultiplexer_1_out2), .Q(r2), .clk(clock), .clr(Reset));
  Register #(.width(16)) register_4 (.D(regval), .en(demultiplexer_1_out3), .Q(r3), .clk(clock), .clr(Reset));
  Register #(.width(16)) register_5 (.D(regval), .en(demultiplexer_1_out4), .Q(r4), .clk(clock), .clr(Reset));
  Register #(.width(16)) register_6 (.D(regval), .en(demultiplexer_1_out5), .Q(r5), .clk(clock), .clr(Reset));
  Register #(.width(16)) register_7 (.D(regval), .en(demultiplexer_1_out6), .Q(r6), .clk(clock), .clr(Reset));
  Register #(.width(16)) register_8 (.D(regval), .en(demultiplexer_1_out7), .Q(r7), .clk(clock), .clr(Reset));
  Multiplexer #(.select(3), .width(16)) multiplexer_1 (
    .in0(r0), .in1(r1), .in2(r2), .in3(r3), .in4(r4), .in5(r5), .in6(r6), .in7(r7), .out(dreg), .sel(dsel));
  Multiplexer #(.select(3), .width(16)) multiplexer_2 (
    .in0(r0), .in1(r1), .in2(r2), .in3(r3), .in4(r4), .in5(r5), .in6(r6), .in7(r7), .out(sreg), .sel(ssel));
  Multiplexer #(.select(3), .width(16)) multiplexer_3 (
    .in0(r0), .in1(r1), .in2(r2), .in3(r3), .in4(r4), .in5(r5), .in6(r6), .in7(r7), .out(treg), .sel(tsel));

  // Notes on the sheet:
  //   Register File
endmodule

module ALU (
  input  [15:0] A,
  input  [15:0] B,
  input  [3:0] aluop,
  output Carry,
  output Zero,
  output Negative,
  output [15:0] Result
);

  wire adder_1_cout, or_2_out, subtractor_1_bout;
  wire [15:0] adder_1_out, and_1_out, divider_1_out, divider_1_rem, multiplier_1_out, nand_1_out, nor_1_out,
       not_1_out, or_1_out, shifter_1_out, shifter_2_out, shifter_3_out, shifter_4_out, shifter_5_out,
       subtractor_1_out, xor_1_out;

  Adder #(.width(16)) adder_1 (.a(A), .b(B), .out(adder_1_out), .cin(1'b0), .cout(adder_1_cout));
  Subtractor #(.width(16)) subtractor_1 (.a(A), .b(B), .out(subtractor_1_out), .bin(1'b0), .bout(subtractor_1_bout));
  Multiplier #(.width(16)) multiplier_1 (.a(A), .b(B), .out(multiplier_1_out), .cin({16{1'b0}}));  // open: cout
  Divider #(.width(16)) divider_1 (.a(A), .b(B), .out(divider_1_out), .upper({16{1'b0}}), .rem(divider_1_rem));
  assign and_1_out = A & B;  // AND_Gate and_1, 16 bits wide
  assign or_1_out = A | B;  // OR_Gate or_1, 16 bits wide
  assign xor_1_out = A ^ B;  // XOR_Gate xor_1, 16 bits wide
  assign nand_1_out = ~(A & B);  // NAND_Gate nand_1, 16 bits wide
  assign nor_1_out = ~(A | B);  // NOR_Gate nor_1, 16 bits wide
  assign not_1_out = ~A;  // NOT_Gate not_1, 16 bits wide
  Shifter #(.width(16)) shifter_1 (.in(A), .\dist (B[3:0]), .out(shifter_1_out));
  Shifter #(.shift("lr"), .width(16)) shifter_2 (.in(A), .\dist (B[3:0]), .out(shifter_2_out));
  Shifter #(.shift("ar"), .width(16)) shifter_3 (.in(A), .\dist (B[3:0]), .out(shifter_3_out));
  Shifter #(.shift("rl"), .width(16)) shifter_4 (.in(A), .\dist (B[3:0]), .out(shifter_4_out));
  Shifter #(.shift("rr"), .width(16)) shifter_5 (.in(A), .\dist (B[3:0]), .out(shifter_5_out));
  Multiplexer #(.select(4), .width(16)) multiplexer_1 (
    .in0(adder_1_out), .in1(subtractor_1_out), .in2(multiplier_1_out), .in3(divider_1_out),
    .in4(divider_1_rem), .in5(and_1_out), .in6(or_1_out), .in7(xor_1_out), .in8(nand_1_out), .in9(nor_1_out),
    .in10(not_1_out), .in11(shifter_1_out), .in12(shifter_2_out), .in13(shifter_3_out), .in14(shifter_4_out),
    .in15(shifter_5_out), .out({Negative, Result[14:0]}), .sel(aluop));
  Multiplexer #(.select(4)) multiplexer_2 (
    .in0(adder_1_cout), .in1(subtractor_1_bout), .in2(1'b0), .in3(1'b0), .in4(1'b0), .in5(1'b0), .in6(1'b0),
    .in7(1'b0), .in8(1'b0), .in9(1'b0), .in10(1'b0), .in11(1'b0), .in12(1'b0), .in13(1'b0), .in14(1'b0),
    .in15(1'b0), .out(Carry), .sel(aluop));
  or or_2 (or_2_out, Result[0], Result[1], Result[2], Result[3], Result[4], Result[5], Result[6], Result[7], Result[9], Result[10], Result[11], Result[12], Result[13], Result[14], Negative, Result[8]);
  not not_2 (Zero, or_2_out);

  assign Result[15] = Negative;

  // Notes on the sheet:
  //   16-bit ALU
endmodule

module PC (
  input  [15:0] imreg,
  input  pcload,
  input  clock,
  input  reset,
  input  [15:0] sreg,
  input  [1:0] pcsel,
  output [15:0] pcout
);

  wire [15:0] adder_1_out, adder_2_out, multiplexer_1_out;

  Adder #(.width(16)) adder_1 (.a(pcout), .b(16'h1), .out(adder_1_out));  // open: cin, cout
  Adder #(.width(16)) adder_2 (.a(pcout), .b(imreg), .out(adder_2_out));  // open: cin, cout
  Multiplexer #(.select(2), .width(16)) multiplexer_1 (
    .in0(adder_1_out), .in1(imreg), .in2(adder_2_out), .in3(sreg), .out(multiplexer_1_out), .sel(pcsel));
  Register #(.width(16)) register_1 (.D(multiplexer_1_out), .en(pcload), .Q(pcout), .clk(clock), .clr(reset));

  // Notes on the sheet:
  //   PC Logic
endmodule

module ShowHexa (
  input  [15:0] Data,
  output [3:0] out_2,
  output [3:0] out_3,
  output [3:0] Digit,
  output [3:0] out_5
);


  assign Digit = Data[7:4];
  assign out_2 = Data[15:12];
  assign out_3 = Data[11:8];
  assign out_5 = Data[3:0];
endmodule

module Frame_Buffer_16x16 (
  input  [3:0] address,
  input  store,
  input  [15:0] data,
  input  clock,
  input  reset,
  output [15:0] out_6,
  output [15:0] out_7,
  output [15:0] out_8,
  output [15:0] out_9,
  output [15:0] out_10,
  output [15:0] out_11,
  output [15:0] out_12,
  output [15:0] out_13,
  output [15:0] out_14,
  output [15:0] out_15,
  output [15:0] out_16,
  output [15:0] out_17,
  output [15:0] out_18,
  output [15:0] out_19,
  output [15:0] out_20,
  output [15:0] out_21
);

  wire demultiplexer_1_out0, demultiplexer_1_out1, demultiplexer_1_out2, demultiplexer_1_out3,
       demultiplexer_1_out4, demultiplexer_1_out5, demultiplexer_1_out6, demultiplexer_1_out7,
       demultiplexer_1_out8, demultiplexer_1_out9, demultiplexer_1_out10, demultiplexer_1_out11,
       demultiplexer_1_out12, demultiplexer_1_out13, demultiplexer_1_out14, demultiplexer_1_out15;

  Demultiplexer #(.select(4)) demultiplexer_1 (
    .out0(demultiplexer_1_out0), .out1(demultiplexer_1_out1), .out2(demultiplexer_1_out2),
    .out3(demultiplexer_1_out3), .out4(demultiplexer_1_out4), .out5(demultiplexer_1_out5),
    .out6(demultiplexer_1_out6), .out7(demultiplexer_1_out7), .out8(demultiplexer_1_out8),
    .out9(demultiplexer_1_out9), .out10(demultiplexer_1_out10), .out11(demultiplexer_1_out11),
    .out12(demultiplexer_1_out12), .out13(demultiplexer_1_out13), .out14(demultiplexer_1_out14),
    .out15(demultiplexer_1_out15), .in(store), .sel(address));
  Register #(.width(16)) register_1 (.D(data), .en(demultiplexer_1_out0), .Q(out_6), .clk(clock), .clr(reset));
  Register #(.width(16)) register_2 (.D(data), .en(demultiplexer_1_out1), .Q(out_7), .clk(clock), .clr(reset));
  Register #(.width(16)) register_3 (.D(data), .en(demultiplexer_1_out2), .Q(out_8), .clk(clock), .clr(reset));
  Register #(.width(16)) register_4 (.D(data), .en(demultiplexer_1_out3), .Q(out_9), .clk(clock), .clr(reset));
  Register #(.width(16)) register_5 (.D(data), .en(demultiplexer_1_out4), .Q(out_10), .clk(clock), .clr(reset));
  Register #(.width(16)) register_6 (.D(data), .en(demultiplexer_1_out5), .Q(out_11), .clk(clock), .clr(reset));
  Register #(.width(16)) register_7 (.D(data), .en(demultiplexer_1_out6), .Q(out_12), .clk(clock), .clr(reset));
  Register #(.width(16)) register_8 (.D(data), .en(demultiplexer_1_out7), .Q(out_13), .clk(clock), .clr(reset));
  Register #(.width(16)) register_9 (.D(data), .en(demultiplexer_1_out8), .Q(out_14), .clk(clock), .clr(reset));
  Register #(.width(16)) register_10 (.D(data), .en(demultiplexer_1_out9), .Q(out_15), .clk(clock), .clr(reset));
  Register #(.width(16)) register_11 (.D(data), .en(demultiplexer_1_out10), .Q(out_16), .clk(clock), .clr(reset));
  Register #(.width(16)) register_12 (.D(data), .en(demultiplexer_1_out11), .Q(out_17), .clk(clock), .clr(reset));
  Register #(.width(16)) register_13 (.D(data), .en(demultiplexer_1_out12), .Q(out_18), .clk(clock), .clr(reset));
  Register #(.width(16)) register_14 (.D(data), .en(demultiplexer_1_out13), .Q(out_19), .clk(clock), .clr(reset));
  Register #(.width(16)) register_15 (.D(data), .en(demultiplexer_1_out14), .Q(out_20), .clk(clock), .clr(reset));
  Register #(.width(16)) register_16 (.D(data), .en(demultiplexer_1_out15), .Q(out_21), .clk(clock), .clr(reset));
endmodule

module Address_Decoder (
  input  [15:0] Address,
  input  in_2,
  input  in_3,
  output RAM,
  output FB_LED,
  output TTY,
  output output_3
);

  Decoder #(.select(2)) decoder_1 (
    .out0(RAM), .out1(FB_LED), .out2(TTY), .out3(output_3), .sel(Address[15:14]), .en(1'b1));
endmodule

module Counters (
  input  [1:0] new_ucounter,
  input  reset,
  input  clock,
  output [15:0] cycles,
  output [3:0] icycles,
  output [15:0] cmds
);

  wire nor_1_out;

  nor nor_1 (nor_1_out, new_ucounter[0], new_ucounter[1]);
  Counter #(.max('hffff), .width(16)) counter_1 (
    .Q(cycles), .clk(clock), .clr(reset));  // open: load, D, count, carry, up
  Counter #(.max('hf), .width(4)) counter_2 (
    .load(nor_1_out), .D(4'b0000), .Q(icycles), .clk(clock), .clr(reset));  // open: count, carry, up
  Counter #(.max('hffff), .width(16)) counter_3 (
    .count(nor_1_out), .Q(cmds), .clk(clock), .clr(reset));  // open: load, D, carry, up
  // Probe on cycles
  // Probe on icycles
  // Probe on cmds

  // Notes on the sheet:
  //   Counts the number of clock cycles
  //   since the start.
  //   Counts the number of clock cycles
  //   since the start of current instruction.
  //   Counts the number of instructions
  //   since the start.
  //   Cycle/Cmds Counters
endmodule

module DebugUnit (
  input  reset,
  input  \continue ,
  input  clock,
  input  [15:0] pcreg,
  input  [15:0] break_addr,
  input  break_on_addr,
  input  [1:0] ucounter,
  input  break_on_instr,
  input  break_on_cycle,
  output clock_out
);

  wire and_1_out, and_2_out, and_3_out, nor_1_out, nor_2_out, nor_3_out, or_1_out, shift_register_1_out,
       shift_register_1_q0;
  wire [15:0] xor_1_out;

  Shift_Register #(.length(2), .trigger("falling")) shift_register_1 (
    .in(\continue ), .clk(clock), .out(shift_register_1_out), .clr(reset), .q0(shift_register_1_q0));  // open: shift, load, d0, d1, q1
  assign xor_1_out = pcreg ^ break_addr;  // XOR_Gate xor_1, 16 bits wide
  LED Addr (.in(break_on_addr));
  and and_1 (and_1_out, ~shift_register_1_out, shift_register_1_q0);  // AND_Gate
  nor nor_1 (nor_1_out, xor_1_out[15], xor_1_out[14], xor_1_out[13], xor_1_out[12], xor_1_out[11], xor_1_out[10], xor_1_out[9], xor_1_out[8], xor_1_out[6], xor_1_out[5], xor_1_out[4], xor_1_out[3], xor_1_out[2], xor_1_out[1], xor_1_out[0], xor_1_out[7]);
  and and_2 (and_2_out, nor_1_out, break_on_addr, nor_2_out);
  nor nor_2 (nor_2_out, ucounter[0], ucounter[1]);
  and and_3 (and_3_out, nor_2_out, break_on_instr);
  LED Instr (.in(break_on_instr));
  LED Cycle (.in(break_on_cycle));
  nor nor_3 (nor_3_out, and_2_out, and_3_out, break_on_cycle);
  or or_1 (or_1_out, and_1_out, nor_3_out);
  LED Pass (.in(or_1_out));
  and and_4 (clock_out, clock, or_1_out);

  // Notes on the sheet:
  //   Breaks on PC = break_addr
  //   Breaks on each new instruction
  //   Breaks on each clock pulse
  //   Makes sure the 'continue' button only
  //   lets through 1 clock pulse, until you let go
  //   and press it again.
  //   Outputs 1 only on first cycle (shift bits are unequal).
  //   Debug Unit
  //   PC = break_addr?
endmodule

module ImmediateReg (
  input  [15:0] DataIn,
  input  IMLoad,
  input  CLKin,
  output [15:0] ImmOut
);

  Register #(.width(16)) register_1 (.D(DataIn), .en(IMLoad), .Q(ImmOut), .clk(CLKin));  // open: clr
  // Probe on ImmOut
endmodule

module ControlUnit_HW (
  input  [6:0] opcode,
  input  c,
  input  z,
  input  n,
  input  clock,
  output [1:0] phase,
  output swrite,
  output irload,
  output imload,
  output dwrite,
  output [1:0] regsrc,
  output datawrite,
  output [1:0] addrsel,
  output [3:0] aluop,
  output [1:0] datasel,
  output pcload,
  output [1:0] op2sel,
  output [1:0] pcsel
);

  wire and_1_out, and_2_out, and_3_out, and_4_out, and_5_out, and_6_out, and_7_out, and_8_out, and_9_out,
       and_10_out, and_11_out, not_1_out, not_2_out, not_3_out, not_4_out, not_5_out, not_6_out, not_7_out,
       not_8_out, not_9_out, not_10_out, not_11_out, not_12_out, not_13_out, or_1_out, or_2_out, or_3_out,
       or_4_out;

  not not_1 (not_1_out, opcode[5]);
  not not_2 (not_2_out, opcode[6]);
  not not_3 (not_3_out, opcode[1]);
  not not_4 (not_4_out, opcode[4]);
  not not_5 (not_5_out, opcode[4]);
  not not_6 (not_6_out, z);
  not not_7 (not_7_out, opcode[4]);
  Multiplexer #(.select(2)) multiplexer_1 (.in0(1'b1), .in1(1'b0), .in2(1'b0), .in3(1'b0), .out(irload), .sel(phase));
  and and_1 (and_1_out, not_1_out, not_2_out);
  and and_2 (and_2_out, opcode[5], opcode[4]);
  and and_3 (and_3_out, opcode[0], not_3_out);
  and and_4 (and_4_out, opcode[5], opcode[3], not_4_out);
  and and_5 (and_5_out, opcode[5], opcode[3], not_5_out);
  and and_6 (and_6_out, not_6_out, opcode[5], opcode[3], not_7_out);
  or or_1 (or_1_out, and_1_out, and_2_out);
  or or_2 (or_2_out, and_3_out, and_4_out);
  Multiplexer #(.select(2)) multiplexer_2 (
    .in0(1'b0), .in1(1'b0), .in2(and_5_out), .in3(1'b0), .out(op2sel[1]), .sel(phase));
  Multiplexer #(.select(2)) multiplexer_3 (
    .in0(1'b0), .in1(1'b0), .in2(and_6_out), .in3(1'b0), .out(pcsel[0]), .sel(phase));
  Multiplexer #(.select(2)) multiplexer_4 (
    .in0(1'b0), .in1(1'b0), .in2(or_1_out), .in3(1'b0), .out(dwrite), .sel(phase));
  Multiplexer #(.select(2)) multiplexer_5 (
    .in0(1'b0), .in1(1'b0), .in2(or_2_out), .in3(1'b0), .out(aluop[0]), .sel(phase));
  not not_8 (not_8_out, opcode[4]);
  and and_7 (and_7_out, opcode[5], opcode[3], not_8_out);
  not not_9 (not_9_out, opcode[5]);
  not not_10 (not_10_out, opcode[6]);
  not not_11 (not_11_out, z);
  Counter #(.max('h3), .width(2)) counter_1 (
    .Q(phase), .up(1'b1), .clk(clock), .clr(and_8_out));  // open: load, D, count, carry
  and and_8 (and_8_out, phase[1], phase[0]);
  or or_3 (or_3_out, opcode[6], and_7_out);
  and and_9 (and_9_out, not_9_out, not_10_out);
  and and_10 (and_10_out, opcode[5], not_12_out);
  not not_12 (not_12_out, opcode[6]);
  and and_11 (and_11_out, not_11_out, opcode[5], not_13_out);
  not not_13 (not_13_out, opcode[6]);
  Multiplexer #(.select(2)) multiplexer_6 (
    .in0(1'b0), .in1(or_3_out), .in2(1'b0), .in3(1'b0), .out(imload), .sel(phase));
  Multiplexer #(.select(2)) multiplexer_7 (
    .in0(1'b0), .in1(1'b0), .in2(and_9_out), .in3(1'b0), .out(regsrc[1]), .sel(phase));
  Multiplexer #(.select(2)) multiplexer_8 (
    .in0(1'b0), .in1(1'b0), .in2(opcode[6]), .in3(1'b0), .out(addrsel[0]), .sel(phase));
  or or_4 (or_4_out, and_10_out, and_11_out);
  Multiplexer #(.select(2)) multiplexer_9 (
    .in0(1'b1), .in1(opcode[6]), .in2(or_4_out), .in3(1'b0), .out(pcload), .sel(phase));

  assign addrsel[1] = 1'b0;
  assign aluop[3:1] = 3'b000;
  assign datasel = {1'b0, addrsel[0]};
  assign datawrite = addrsel[0];
  assign op2sel[0] = 1'b0;
  assign pcsel[1] = 1'b0;
  assign regsrc[0] = 1'b0;
  assign swrite = 1'b0;

  // Other names for the same wires on the sheet: carry = c; neg = n; b0 = opcode[0]; b1 = opcode[1]; b2 = opcode[2];
  //   b3 = opcode[3]; b4 = opcode[4]; b5 = opcode[5]; b6 = opcode[6]; zero = z

  // Notes on the sheet:
  //   IR Load
  //   Dwrite
  //   Aluop
  //   Op2sel
  //   Pc Select
  //   Phase counter
  //   Immed Load
  //   Regsrc
  //   Addrsel, Datawrite, datasel
  //   Pc Load
endmodule
